# Fritzing sketch step1 (saved by Fritzing 0.9.2b)
circuit board: 8.46667cm x 5.64444cm
breadboards: 1

parts:
  Componente1 = Arduino Uno (Rev3)
  R1 = Resistor [tolerance=±5% resistance=220 package=THT]
  R2 = Resistor [tolerance=±5% resistance=220 package=THT]
  LED1 = LED - 5mm [color="Red (633nm)" package="5 mm [THT]"]
  LED2 = LED - 5mm [color="Red (633nm)" package="5 mm [THT]"]

nets:
  N1: Componente1.D10_PWM/SS, R1.Pin_1
  N2: Componente1.GND, LED1.cathode, LED2.cathode
  N3: Componente1.D4, R2.Pin_1
  N4: R1.Pin_0, LED1.anode
  N5: R2.Pin_0, LED2.anode
